# Fritzing sketch hit_the_mole (saved by Fritzing 0.9.3b)
breadboards: 1

parts:
  Part2 = Arduino Uno (Rev3)
  LED5 = LED - 5mm [color="Yellow (595nm)" package="5 mm [THT]"]
  LED6 = LED - 5mm [color="Red (633nm)" package="5 mm [THT]"]
  LED7 = LED - 5mm [color="Red (660nm)" package="5 mm [THT]"]
  LED8 = LED - 5mm [color="Green (570nm)" package="5 mm [THT]"]
  R5 = Resistor [tolerance=±5% resistance=220 package=THT]
  R6 = Resistor [tolerance=±5% resistance=220 package=THT]
  R7 = Resistor [tolerance=±5% resistance=220 package=THT]
  R8 = Resistor [tolerance=±5% resistance=220 package=THT]
  S5 = Pushbutton [package="[THT]"]
  S6 = Pushbutton [package="[THT]"]
  S7 = Pushbutton [package="[THT]"]
  S8 = Pushbutton [package="[THT]"]

nets:
  N1: Part2.D9_PWM, R5.Pin_1
  N2: Part2.D10_PWM/SS, R6.Pin_1
  N3: Part2.D11_PWM/MOSI, R7.Pin_0
  N4: Part2.D12/MISO, R8.Pin_1
  N5: Part2.GND, LED5.cathode, LED6.cathode, LED7.cathode, LED8.cathode, S5.Pin_1, S5.Pin_2, S6.Pin_1, S6.Pin_2, S7.Pin_1, S7.Pin_2, S8.Pin_1, S8.Pin_2
  N6: Part2.D4, S8.Pin_3, S8.Pin_4
  N7: Part2.D5_PWM, S7.Pin_3, S7.Pin_4
  N8: Part2.D6_PWM, S6.Pin_3, S6.Pin_4
  N9: Part2.D7, S5.Pin_3, S5.Pin_4
  N10: LED5.anode, R8.Pin_0
  N11: LED6.anode, R7.Pin_1
  N12: LED7.anode, R6.Pin_0
  N13: LED8.anode, R5.Pin_0

// code stored in the sketch: gwctv_whack_a_mole.ino
const int yellowLED = 12;
const int redLED = 11;
const int pinkLED = 10;
const int greenLED = 9;

const int yellowButton = 7;
const int redButton = 6;
const int pinkButton = 5;
const int greenButton = 4;

int waitTime = 3000; 
int counter = 1;

void setup() {
  
  pinMode(yellowLED, OUTPUT);
  pinMode(redLED, OUTPUT);
  pinMode(pinkLED, OUTPUT);
  pinMode(greenLED, OUTPUT);
  pinMode(yellowButton, INPUT_PULLUP);
  pinMode(redButton, INPUT_PULLUP);
  pinMode(pinkButton, INPUT_PULLUP);
  pinMode(greenButton, INPUT_PULLUP);
  
  Serial.begin(9600);      // serial port = 9600 bps
  randomSeed(analogRead(0));   //shows random numbers are truly random
}

void loop() {
  int newColor = randomLED();
  ledOn(newColor);

  //check to see if hit or not
  if (hit(newColor)) {
    Serial.print("No. of mole hit:");
    Serial.println(counter);
    ledOff(newColor);
    delay(1000); 
    waitTime = 0.9*waitTime;
    counter++;
  } else {
    Serial.println("Miss the mole! Game over.");
    miss();
    waitTime = 3000;               // 1 sec = 1000 milisecond
    counter = 1;
  } 
}

boolean hit(int newColor) {
  int i = 0;
  int chkButton;
  boolean hit = false;
  boolean buttonPressed = false;

  //start the counter and wait for botton to be pressed..or timeout
  Serial.print("Wait Time: ");
  Serial.println(waitTime);
  while ((i < waitTime) and (!buttonPressed)) {
    
    chkButton = button(); //0 if nothing is pressed
    if (newColor == chkButton) { //correct button is pressed
      hit = true;
      buttonPressed = true;
    } else if (chkButton > 0) { //incorrect button is pressed
      hit = false;
      buttonPressed = true;
    } 
    i++;
    delay(1); //make each loop about 1ms
  }
  return hit;
}

 // 7 = yellow,6 = red, 5 = pink, 4=green
 //LOW = button is pressed
int button() {
    int buttonPressed = 0;
    if (digitalRead(yellowButton) == LOW) {
      ledOn(yellowLED);
      buttonPressed = yellowLED;
    }
    if (digitalRead(redButton) == LOW) {
      ledOn(redLED);
      buttonPressed = redLED;
    } 
    if (digitalRead(pinkButton) == LOW) {
      ledOn(pinkLED);
      buttonPressed = pinkLED;
    }  
    if (digitalRead(greenButton) == LOW) {
      ledOn(greenLED);
      buttonPressed = greenLED;
    }
    return buttonPressed;
}

void miss() {
  
   for (int i=0; i <= 2; i++){
     ledOn(yellowLED);
     ledOn(redLED);
     ledOn(pinkLED);
     ledOn(greenLED);
     delay(200);
     ledOff(yellowLED);
     ledOff(redLED);
     ledOff(pinkLED);
     ledOff(greenLED);
     delay(200);
   }
  delay(2000);
}  

//function shows to randomly pick a new color of LED
int randomLED () {
  int randomLED;
  randomLED = random(9,13);
  return randomLED;

}
void ledOn(int colorON) {

  if (colorON == yellowLED) {
    digitalWrite(yellowLED, HIGH);
  }
  else if (colorON == redLED) {
    digitalWrite(redLED, HIGH);
  }
  else if (colorON == pinkLED) {
    digitalWrite(pinkLED, HIGH);
  } 
  else if (colorON == greenLED) {
    digitalWrite(greenLED, HIGH);
  }
}

void ledOff(int colorOFF) {

  if (colorOFF == yellowLED) {
    digitalWrite(yellowLED, LOW);
  }
  else if (colorOFF == redLED) {
    digitalWrite(redLED, LOW);
  }
  else if (colorOFF == pinkLED) {
    digitalWrite(pinkLED, LOW);
  }
  else if (colorOFF == greenLED) {
    digitalWrite(greenLED, LOW);
  }
}
